# Fritzing sketch ESPLogger (saved by Fritzing 0.9.2b)
circuit board: 5.57278cm x 5.52206cm
perfboards: 1

parts:
  U1 = ESP8266 WiFi Module [part_number=ESP8266]
  R1 = Resistor [tolerance=±5% resistance=100 package=THT]
  U2 = mystery part, 3 pins [chip_label=DHT22]
  R2 = Resistor [tolerance=±5% resistance=2.2k package=THT]
  R3 = Resistor [tolerance=±5% resistance=2.2k package=THT]
  R4 = Resistor [tolerance=±5% resistance=1k package=THT]
  U3 = mystery part, 4 pins [chip_label=Lux]
  C1 = Electrolytic Capacitor [capacitance=4.7µF voltage=16V package="100 mil [THT, electrolytic]"]
  R5 = Resistor [tolerance=±5% resistance=2.2k package=THT]
  R6 = Resistor [tolerance=±5% resistance=2.2k package=THT]
  V2 = DC Power [voltage=3.3V]
  D1 = Rectifier Diode [part_number=1N4001 package="300 mil [THT]"]
  S1 = Pushbutton [package="[THT]"]

nets:
  5V: U1.VCC, U2.pin1, R2.Pin_0, R3.Pin_0, R4.Pin_1, C1.+, V2.V+, D1.anode
  N1: U1.GPIO_0, R6.Pin_1
  N2: U1.GPIO_2, R3.Pin_1
  N3: U1.CH_PD, R2.Pin_1
  N4: U1.GPIO_15, R5.Pin_0
  N5: U1.GPIO_16, R1.Pin_0
  N6: U1.GPIO_14, U3.pin4
  N7: U1.GPIO_12, U3.pin3
  N8: U1.GPIO_13, U2.pin2, R4.Pin_0
  N9: U1.REST, R1.Pin_1
  GND: U2.pin3, U3.pin2, C1.-, R5.Pin_1, V2.V-, S1.Pin_1, S1.Pin_2
  N10: U3.pin1, D1.cathode
  N11: R6.Pin_0, S1.Pin_3, S1.Pin_4
